# Fritzing sketch smart-irrigation (saved by Fritzing 1.0.0d)

parts:
  Mod1 = Amica NodeMCU DEVKIT 1.0
  YF-S201_Flow_Meter2 = YF-S201 Water Flow Meter
  VALVE1 = Plastic Solenoid Valve
  KY-1 = Keyes Relay [package=THT]
  HC-SR04_Sensor_1 = HC-SR04 Ultrasonic Distance Sensor
  3V3_OUT = RioRand LM2596
  SIM800L1 = SIM800L
  R1 = Resistor [tolerance=±5% resistance=10k package="2010 [SMD]"]
  R2 = Resistor [tolerance=±5% resistance=20k package="2010 [SMD]"]
  12V_VIN = Power Jack [package=power_jack_slot]
  5V_OUT = RioRand LM2596

nets:
  GND: Mod1.pin2, Mod1.pin_9, Mod1.pin_25, Mod1.pin_29, YF-S201_Flow_Meter2.GND, KY-1.ground, HC-SR04_Sensor_1.GND, R2.Pin_1, 5V_OUT.Pin_4
  N1: Mod1.pin8, R1.Pin_0
  N2: Mod1.pin_11, SIM800L1.TXD
  N3: Mod1.pin_12, HC-SR04_Sensor_1.ECHO
  N4: Mod1.pin_13, HC-SR04_Sensor_1.TRIG
  N5: Mod1.pin_14, YF-S201_Flow_Meter2.SIG
  N6: Mod1.pin_15, KY-1.signal
  VCC: Mod1.pin_30, YF-S201_Flow_Meter2.VCC, KY-1.power, HC-SR04_Sensor_1.VCC, 5V_OUT.Pin_3
  N7: VALVE1.no_name_yet#1, 3V3_OUT.Pin_2, 12V_VIN.GND, 5V_OUT.Pin_2
  N8: VALVE1.no_name_yet#2, KY-1.NO
  N9: KY-1.C, 3V3_OUT.Pin_1, 12V_VIN.PWR, 5V_OUT.Pin_1
  N10: 3V3_OUT.Pin_3, SIM800L1.VCC
  N11: 3V3_OUT.Pin_4, SIM800L1.GND
  N12: SIM800L1.RXD, R1.Pin_1, R2.Pin_0

custom parts:
  YF-S201 Water Flow Meter: The YF-S201 Flow Meter. The input voltage is 5V to 24V (DC).
  Keyes Relay: The Keyes 5V relay module is suitable for SCM development, home appliance control. It uses a 5V~12V TIL control signal which can control DC / AC signal.
  SIM800L: SIM800L is a miniature cellular module which allows for GPRS transmission, sending and receiving SMS and making and receiving voice calls. Low cost and small footprint and quad band frequency support make this module perfect solution for any project that require long range connectivity. After connecting power module boots up, searches for cellular network and login automatically. On board LED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
